# Fritzing sketch LED cube breadboard (saved by Fritzing 0.9.4)
breadboards: 2

parts:
  Raspberry_Pi1 = Raspberry Pi 2
  Q1 = Basic FET N-Channel [package="TO220 [THT]"]
  Q2 = Basic FET N-Channel [package="TO220 [THT]"]
  R1 = Resistor [tolerance=±5% resistance=330 package=THT]
  R2 = Resistor [tolerance=±5% resistance=330 package=THT]
  R3 = Resistor [tolerance=±10% resistance=330 package=THT]
  R4 = Resistor [tolerance=±5% resistance=330 package=THT]
  Q3 = Basic FET N-Channel [package="TO220 [THT]"]
  Q4 = Basic FET N-Channel [package="TO220 [THT]"]

nets:
  N1: Raspberry_Pi1.GPIO19, Q3.source
  N2: Raspberry_Pi1.GPIO26, Q4.source
  N3: Raspberry_Pi1.GPIO20, Q2.source
  N4: Raspberry_Pi1.GPIO16, Q1.source
  N5: Raspberry_Pi1.GND, Q1.gate, Q2.gate, Q3.gate, Q4.gate
  N6: Q1.drain, R1.Pin_1
  N7: Q2.drain, R4.Pin_0
  N8: R2.Pin_0, Q3.drain
  N9: R3.Pin_0, Q4.drain

notes:
  Break out board
  cathodes - orange
  anodes - purple
  neither rhyme :'D
  [my resistors are half the length of those in this diagram]
  row connected to self show where LEDs plugged in
  TODO: buy dupont socket-plug dupont wires to get ride of this breakout board
