# Fritzing sketch ArduinoDemux (saved by Fritzing 0.9.4)
breadboards: 1

parts:
  IC1 = IC, DIP package, 16 pins [chip_label=CD4051BE]
  LED1 = LED - 5mm [color="Red (633nm)" package="5 mm [THT]"]
  LED2 = LED - 5mm [color="Red (633nm)" package="5 mm [THT]"]
  LED3 = LED - 5mm [color="Red (633nm)" package="5 mm [THT]"]
  LED4 = LED - 5mm [color="Red (633nm)" package="5 mm [THT]"]
  LED5 = LED - 5mm [color="Red (633nm)" package="5 mm [THT]"]
  LED6 = LED - 5mm [color="Red (633nm)" package="5 mm [THT]"]
  LED7 = LED - 5mm [color="Red (633nm)" package="5 mm [THT]"]
  LED8 = LED - 5mm [color="Red (633nm)" package="5 mm [THT]"]
  R1 = Resistor [tolerance=±5% resistance=220 package=THT]
  R2 = Resistor [tolerance=±5% resistance=220 package=THT]
  R3 = Resistor [tolerance=±5% resistance=220 package=THT]
  R4 = Resistor [tolerance=±5% resistance=220 package=THT]
  R5 = Resistor [tolerance=±5% resistance=220 package=THT]
  R6 = Resistor [tolerance=±5% resistance=220 package=THT]
  R7 = Resistor [tolerance=±5% resistance=220 package=THT]
  R8 = Resistor [tolerance=±5% resistance=220 package=THT]
  Part1 = Arduino Uno (Rev3)

nets:
  N1: IC1.pin1, LED5.anode
  N2: IC1.pin2, LED7.anode
  N3: IC1.pin3, Part1.D11_PWM/MOSI
  N4: IC1.pin4, LED8.anode
  N5: IC1.pin5, LED6.anode
  N6: IC1.pin8, R1.Pin_1, R2.Pin_1, R3.Pin_1, R4.Pin_1, R5.Pin_1, R6.Pin_1, R7.Pin_1, R8.Pin_1, Part1.GND
  N7: IC1.pin9, Part1.D4
  N8: IC1.pin10, Part1.D3_PWM
  N9: IC1.pin11, Part1.D2
  N10: IC1.pin12, LED4.anode
  N11: IC1.pin13, LED1.anode
  N12: IC1.pin14, LED2.anode
  N13: IC1.pin15, LED3.anode
  N14: IC1.pin16, Part1.5V
  N15: LED1.cathode, R8.Pin_0
  N16: LED2.cathode, R7.Pin_0
  N17: LED3.cathode, R6.Pin_0
  N18: LED4.cathode, R5.Pin_0
  N19: LED5.cathode, R4.Pin_0
  N20: LED6.cathode, R3.Pin_0
  N21: LED7.cathode, R2.Pin_0
