# Fritzing sketch 3xdemux arduino (saved by Fritzing 0.9.4)
breadboards: 2

parts:
  LED11 = LED - 5mm [color="Red (633nm)" package="5 mm [THT]"]
  LED12 = LED - 5mm [color="Red (633nm)" package="5 mm [THT]"]
  LED13 = smd LED [color="Red (633nm)" package="0603 [SMD]"]
  LED14 = smd LED [color="Red (633nm)" package="0805 [SMD]"]
  LED15 = smd LED [color="Red (633nm)" package="0603 [SMD]"]
  LED16 = LED - 5mm [color="Red (633nm)" package="5 mm [THT]"]
  LED17 = LED - 5mm [color="Red (633nm)" package="5 mm [THT]"]
  LED18 = LED - 5mm [color="Red (633nm)" package="5 mm [THT]"]
  LED19 = LED - 5mm [color="Red (633nm)" package="5 mm [THT]"]
  LED20 = LED - 5mm [color="Red (633nm)" package="5 mm [THT]"]
  LED21 = LED - 5mm [color="Red (633nm)" package="5 mm [THT]"]
  LED22 = LED - 5mm [color="Red (633nm)" package="5 mm [THT]"]
  R11 = Resistor [tolerance=±5% resistance=220 package=THT]
  R12 = Resistor [tolerance=±5% resistance=220 package=THT]
  R13 = Resistor [tolerance=±5% resistance=220 package=THT]
  R14 = Resistor [tolerance=±5% resistance=220 package=THT]
  R15 = Resistor [tolerance=±5% resistance=220 package=THT]
  R16 = Resistor [tolerance=±5% resistance=220 package=THT]
  R17 = Resistor [tolerance=±5% resistance=220 package=THT]
  R18 = Resistor [tolerance=±5% resistance=220 package=THT]
  R19 = Resistor [tolerance=±5% resistance=220 package=THT]
  R20 = Resistor [tolerance=±5% resistance=220 package=THT]
  Part1 = Arduino Uno (Rev3)
  IC1 = IC, DIP package, 16 pins [chip_label=CD4051BE]
  IC2 = IC, DIP package, 16 pins [chip_label=CD4051BE]
  IC3 = IC, DIP package, 16 pins [chip_label=CD4051BE]

nets:
  N1: LED11.cathode, R19.Pin_1
  N2: LED11.anode, IC1.pin15
  N3: LED12.cathode, R16.Pin_1
  N4: LED12.anode, IC1.pin1
  N5: LED13.cathode, LED14.cathode, LED15.cathode, R18.Pin_1
  N6: LED13.anode, LED14.anode, LED15.anode, IC1.pin13
  N7: LED16.cathode, R15.Pin_1
  N8: LED17.anode, IC1.pin14
  N9: LED18.cathode, R14.Pin_1
  N10: LED19.cathode, R11.Pin_1
  N11: LED19.anode, IC1.pin5
  N12: LED20.cathode, R12.Pin_1
  N13: LED20.anode, IC1.pin2
  N14: LED21.cathode, R13.Pin_1
  N15: LED21.anode, IC1.pin4
  N16: LED22.cathode, R20.Pin_1
  N17: LED22.anode, IC1.pin12
  N18: R11.Pin_0, R13.Pin_0, R14.Pin_0, R15.Pin_0, R17.Pin_0, R20.Pin_0, Part1.GND, IC1.pin8, IC2.pin8, IC3.pin8
  N19: Part1.D8, IC3.pin11
  N20: Part1.D9_PWM, IC1.pin3
  N21: Part1.D10_PWM/SS, IC2.pin3
  N22: Part1.D11_PWM/MOSI, IC3.pin3
  N23: Part1.D12/MISO, IC3.pin10
  N24: Part1.D13/SCK, IC3.pin9
  N25: Part1.D2, IC1.pin11
  N26: Part1.D3_PWM, IC1.pin10
  N27: Part1.D4, IC1.pin9
  N28: Part1.D5_PWM, IC2.pin11
  N29: Part1.D6_PWM, IC2.pin10
  N30: Part1.D7, IC2.pin9
  N31: Part1.5V, IC1.pin16, IC2.pin16, IC3.pin16

notes:
  IRL, each of the ICs will have blue output li nes
  2 columns of 12x LEDs
