# Fritzing sketch flashingLEDs (saved by Fritzing 0.9.4)
breadboards: 1

parts:
  Part1 = Arduino Uno (Rev3)
  S2 = Pushbutton [package="[THT]"]
  R3 = Resistor [tolerance=±5% resistance=1k package=THT]
  LED1 = LED - 5mm [color="Red (633nm)" package="5 mm [THT]"]
  R4 = Resistor [tolerance=±5% resistance=220 package=THT]
  LED2 = LED - 5mm [color="Red (633nm)" package="5 mm [THT]"]
  R5 = Resistor [tolerance=±5% resistance=220 package=THT]
  R6 = Resistor [tolerance=±5% resistance=220 package=THT]
  LED3 = LED - 5mm [color="Red (633nm)" package="5 mm [THT]"]
  R7 = Resistor [tolerance=±5% resistance=220 package=THT]
  LED4 = LED - 5mm [color="Red (633nm)" package="5 mm [THT]"]
  R8 = Resistor [tolerance=±5% resistance=220 package=THT]
  LED5 = LED - 5mm [color="Red (633nm)" package="5 mm [THT]"]
  R9 = Resistor [tolerance=±5% resistance=220 package=THT]
  LED6 = LED - 5mm [color="Red (633nm)" package="5 mm [THT]"]
  R2 = Rotary Potentiometer (Small) [maximum_resistance=100kΩ package=THT]

nets:
  N1: Part1.A0, R2.wiper
  N2: Part1.D9_PWM, LED3.anode
  N3: Part1.D10_PWM/SS, LED2.anode
  N4: Part1.D11_PWM/MOSI, LED1.anode
  N5: Part1.D2, S2.Pin_3, S2.Pin_4
  N6: Part1.D3_PWM, LED6.anode
  N7: Part1.D5_PWM, LED5.anode
  N8: Part1.D6_PWM, LED4.anode
  N9: Part1.5V, S2.Pin_1, S2.Pin_2, R2.leg1
  N10: Part1.GND, R3.Pin_0, R5.Pin_0, R6.Pin_0, R7.Pin_0, R9.Pin_0, R2.leg2
  N11: LED1.cathode, R4.Pin_1
  N12: LED2.cathode, R5.Pin_1
  N13: R6.Pin_1, LED3.cathode
  N14: R7.Pin_1, LED4.cathode
  N15: R8.Pin_1, LED5.cathode
  N16: R9.Pin_1, LED6.cathode
