# Fritzing sketch 2strips1pi (saved by Fritzing 0.9.4)
breadboards: 1

parts:
  Raspberry_Pi1 = Raspberry Pi 2
  J1 = Power Jack [package=power_jack_pth]
  IC1 = IC, DIP package, 16 pins [chip_label=CD4051BE]

nets:
  N1: Raspberry_Pi1.GPIO21, IC1.pin11
  N2: Raspberry_Pi1.GPIO18, IC1.pin3
  GND: Raspberry_Pi1.GND, J1.GND, IC1.pin8
  N3: J1.PWR, IC1.pin16

notes:
  Pixel strip 0
  Pixel strip 1
